// Logisim project Labo5_Melly_Rouvinez.circ as structural Verilog: 7 circuits, main circuit COUNT_BASE
module COUNT_BASE (
  input  EN,
  input  CLK,
  output Q,
  output C
);

  wire xor_1_out;

  xor xor_1 (xor_1_out, Q, EN);
  and and_1 (C, Q, EN);
  D_Flip_Flop d_ff_1 (.D(xor_1_out), .clk(CLK), .Q(Q));  // open: Qn, preset, reset

  // Notes on the sheet:
  //   Attention, votre version de Logisim
  //   ne contient pas de tracker. Si vous
  //   enregistrez votre projet, toutes les
  //   informations du tracker seront
  //   définitivement effacées.
endmodule

module COUNT_ALL (
  input  A,
  output [3:0] D
);

  wire CK_out, count_base_1_c, count_base_2_c, count_base_3_c;

  Clock CK (.out(CK_out));
  COUNT_BASE count_base_1 (.EN(A), .CLK(CK_out), .Q(D[0]), .C(count_base_1_c));
  COUNT_BASE count_base_2 (.EN(count_base_1_c), .CLK(CK_out), .Q(D[1]), .C(count_base_2_c));
  COUNT_BASE count_base_3 (.EN(count_base_2_c), .CLK(CK_out), .Q(D[2]), .C(count_base_3_c));
  COUNT_BASE count_base_4 (.EN(count_base_3_c), .CLK(CK_out), .Q(D[3]));  // open: C

  // Notes on the sheet:
  //   Attention, votre version de Logisim
  //   ne contient pas de tracker. Si vous
  //   enregistrez votre projet, toutes les
  //   informations du tracker seront
  //   définitivement effacées.
endmodule

module SHREGI_8BITS (
  input  CLK,
  input  L,
  input  [1:0] S,
  input  [7:0] D,
  input  R,
  input  CLR,
  output [7:0] Q
);

  wire bitselector_1_out, bitselector_2_out;

  SHREGI_4BITS shregi_4bits_1 (.D(D[3:0]), .R(bitselector_1_out), .L(L), .S(S), .CLR(CLR), .CLK(CLK), .Q(Q[3:0]));
  SHREGI_4BITS shregi_4bits_2 (.D(D[7:4]), .R(R), .L(bitselector_2_out), .S(S), .CLR(CLR), .CLK(CLK), .Q(Q[7:4]));
  BitSelector #(.width(4)) bitselector_1 (.in(Q[7:4]), .out(bitselector_1_out), .sel(2'b00));
  BitSelector #(.width(4)) bitselector_2 (.in(Q[3:0]), .out(bitselector_2_out), .sel(2'b11));

  // Notes on the sheet:
  //   Attention, votre version de Logisim
  //   ne contient pas de tracker. Si vous
  //   enregistrez votre projet, toutes les
  //   informations du tracker seront
  //   définitivement effacées.
endmodule

module SHREGI_4BITS (
  input  [3:0] D,
  input  R,
  input  L,
  input  [1:0] S,
  input  CLR,
  input  CLK,
  output [3:0] Q
);

  wire multiplexer_1_out, multiplexer_2_out, multiplexer_3_out, multiplexer_4_out;

  Multiplexer #(.select(2), .enable("false")) multiplexer_1 (
    .in0(Q[3]), .in1(D[3]), .in2(Q[2]), .in3(R), .out(multiplexer_1_out), .sel(S));
  D_Flip_Flop d_ff_1 (.D(multiplexer_1_out), .clk(CLK), .Q(Q[3]), .reset(CLR));  // open: Qn, preset
  Multiplexer #(.select(2), .enable("false")) multiplexer_2 (
    .in0(Q[2]), .in1(D[2]), .in2(Q[1]), .in3(Q[3]), .out(multiplexer_2_out), .sel(S));
  D_Flip_Flop d_ff_2 (.D(multiplexer_2_out), .clk(CLK), .Q(Q[2]), .reset(CLR));  // open: Qn, preset
  Multiplexer #(.select(2), .enable("false")) multiplexer_3 (
    .in0(Q[1]), .in1(D[1]), .in2(Q[0]), .in3(Q[2]), .out(multiplexer_3_out), .sel(S));
  D_Flip_Flop d_ff_3 (.D(multiplexer_3_out), .clk(CLK), .Q(Q[1]), .reset(CLR));  // open: Qn, preset
  Multiplexer #(.select(2), .enable("false")) multiplexer_4 (
    .in0(Q[0]), .in1(D[0]), .in2(L), .in3(Q[1]), .out(multiplexer_4_out), .sel(S));
  D_Flip_Flop d_ff_4 (.D(multiplexer_4_out), .clk(CLK), .Q(Q[0]), .reset(CLR));  // open: Qn, preset

  // Notes on the sheet:
  //   Attention, votre version de Logisim
  //   ne contient pas de tracker. Si vous
  //   enregistrez votre projet, toutes les
  //   informations du tracker seront
  //   définitivement effacées.
endmodule

module UART (
  input  [1:0] in_1,
  input  in_2,
  input  in_3,
  input  in_4,
  output [7:0] out_5
);

  wire and_1_out, clock_1_out;
  wire [1:0] count_4bits_1_d;
  wire [6:0] undriven;

  Clock clock_1 (.out(clock_1_out));
  COUNT_4BITS count_4bits_1 (.A(in_4), .CLK(clock_1_out), .D(count_4bits_1_d));
  and and_1 (and_1_out, count_4bits_1_d[0], count_4bits_1_d[1]);
  SHREGI_8BITS shregi_8bits_1 (.CLK(and_1_out), .S(in_1), .D({in_2, undriven}), .R(in_3), .Q(out_5));  // open: L, CLR

  // Notes on the sheet:
  //   Attention, votre version de Logisim
  //   ne contient pas de tracker. Si vous
  //   enregistrez votre projet, toutes les
  //   informations du tracker seront
  //   définitivement effacées.
endmodule

module COUNT_4BITS (
  input  A,
  input  CLK,
  output [1:0] D
);

  wire count_base_1_c;

  COUNT_BASE count_base_1 (.EN(A), .CLK(CLK), .Q(D[0]), .C(count_base_1_c));
  COUNT_BASE count_base_2 (.EN(count_base_1_c), .CLK(CLK), .Q(D[1]));  // open: C

  // Notes on the sheet:
  //   Attention, votre version de Logisim
  //   ne contient pas de tracker. Si vous
  //   enregistrez votre projet, toutes les
  //   informations du tracker seront
  //   définitivement effacées.
endmodule

module COUNT_8BITS (
  input  A,
  input  CLK,
  output [2:0] out_3
);

  wire count_base_1_c, count_base_2_c;

  COUNT_BASE count_base_1 (.EN(A), .CLK(CLK), .Q(out_3[0]), .C(count_base_1_c));
  COUNT_BASE count_base_2 (.EN(count_base_1_c), .CLK(CLK), .Q(out_3[1]), .C(count_base_2_c));
  COUNT_BASE count_base_3 (.EN(count_base_2_c), .CLK(CLK), .Q(out_3[2]));  // open: C

  // Notes on the sheet:
  //   Attention, votre version de Logisim
  //   ne contient pas de tracker. Si vous
  //   enregistrez votre projet, toutes les
  //   informations du tracker seront
  //   définitivement effacées.
endmodule
